// Logisim project SAP1_8bit_Project.circ as structural Verilog: 19 circuits, main circuit sap1_final_top
module module_testbench (
  input  [7:0] in_1,
  input  in_2,
  input  in_3,
  input  [7:0] in_4,
  input  [7:0] in_5,
  input  in_6,
  input  in_7,
  input  in_8,
  input  in_9,
  input  in_10,
  input  in_11,
  input  in_12,
  input  [7:0] in_13,
  input  in_14,
  input  in_15,
  input  in_16,
  input  in_17,
  input  in_18,
  input  in_19,
  input  in_20,
  output [7:0] out_21,
  output out_22,
  output [7:0] out_23,
  output [7:0] out_24,
  output [7:0] out_25,
  output [3:0] out_26
);

  wire [7:0] register_8bit_1_reg_out, register_8bit_2_reg_out;

  pc_4bit_ripple_lab pc_4bit_ripple_lab_1 (
    .pc_en(in_17), .pc_clk(in_18), .pc_reset(in_19), .pc_out_en(in_20), .pc_value(out_26));  // open: pc_out
  register_8bit register_8bit_1 (
    .reg_in(in_5), .reg_in_en(in_6), .reg_clk(in_7), .reg_out_en(in_8), .reg_out(register_8bit_1_reg_out));  // open: reg_int_out
  register_8bit register_8bit_2 (
    .reg_in(in_5), .reg_in_en(in_11), .reg_clk(in_7), .reg_out_en(in_12), .reg_out(register_8bit_2_reg_out));  // open: reg_int_out
  // alu_8bit alu_8bit_1: pin names not known; wires that end beside it: register_8bit_1_reg_out, in_9, in_10, register_8bit_2_reg_out, out_23
  register_8bit register_8bit_3 (
    .reg_in(in_13), .reg_in_en(in_14), .reg_clk(in_15), .reg_out_en(in_16), .reg_int_out(out_24),
    .reg_out(out_25));
  // alu_8bit alu_8bit_2: pin names not known; wires that end beside it: in_1, in_2, in_3, in_4, out_21, out_22
endmodule

module register_8bit (
  input  [7:0] reg_in,
  input  reg_in_en,
  input  reg_clk,
  input  reg_out_en,
  output [7:0] reg_int_out,
  output [7:0] reg_out
);

  wire multiplexer_1_out, multiplexer_2_out, multiplexer_3_out, multiplexer_4_out, multiplexer_5_out,
       multiplexer_6_out, multiplexer_7_out, multiplexer_8_out;

  Multiplexer multiplexer_1 (.in0(reg_int_out[7]), .in1(reg_in[7]), .out(multiplexer_1_out), .sel(reg_in_en));
  D_Flip_Flop d_ff_1 (.D(multiplexer_1_out), .clk(reg_clk), .Q(reg_int_out[7]));  // open: Qn, preset, reset
  Multiplexer multiplexer_2 (.in0(reg_int_out[6]), .in1(reg_in[6]), .out(multiplexer_2_out), .sel(reg_in_en));
  assign reg_out[7] = reg_out_en ? reg_int_out[7] : 1'bz;  // Controlled_Buffer controlled_buffer_1
  D_Flip_Flop d_ff_2 (.D(multiplexer_2_out), .clk(reg_clk), .Q(reg_int_out[6]));  // open: Qn, preset, reset
  Multiplexer multiplexer_3 (.in0(reg_int_out[5]), .in1(reg_in[5]), .out(multiplexer_3_out), .sel(reg_in_en));
  D_Flip_Flop d_ff_3 (.D(multiplexer_3_out), .clk(reg_clk), .Q(reg_int_out[5]));  // open: Qn, preset, reset
  assign reg_out[6] = reg_out_en ? reg_int_out[6] : 1'bz;  // Controlled_Buffer controlled_buffer_2
  Multiplexer multiplexer_4 (.in0(reg_int_out[4]), .in1(reg_in[4]), .out(multiplexer_4_out), .sel(reg_in_en));
  assign reg_out[5] = reg_out_en ? reg_int_out[5] : 1'bz;  // Controlled_Buffer controlled_buffer_3
  D_Flip_Flop d_ff_4 (.D(multiplexer_4_out), .clk(reg_clk), .Q(reg_int_out[4]));  // open: Qn, preset, reset
  Multiplexer multiplexer_5 (.in0(reg_int_out[3]), .in1(reg_in[3]), .out(multiplexer_5_out), .sel(reg_in_en));
  assign reg_out[4] = reg_out_en ? reg_int_out[4] : 1'bz;  // Controlled_Buffer controlled_buffer_4
  D_Flip_Flop d_ff_5 (.D(multiplexer_5_out), .clk(reg_clk), .Q(reg_int_out[3]));  // open: Qn, preset, reset
  assign reg_out[3] = reg_out_en ? reg_int_out[3] : 1'bz;  // Controlled_Buffer controlled_buffer_5
  Multiplexer multiplexer_6 (.in0(reg_int_out[2]), .in1(reg_in[2]), .out(multiplexer_6_out), .sel(reg_in_en));
  D_Flip_Flop d_ff_6 (.D(multiplexer_6_out), .clk(reg_clk), .Q(reg_int_out[2]));  // open: Qn, preset, reset
  Multiplexer multiplexer_7 (.in0(reg_int_out[1]), .in1(reg_in[1]), .out(multiplexer_7_out), .sel(reg_in_en));
  assign reg_out[2] = reg_out_en ? reg_int_out[2] : 1'bz;  // Controlled_Buffer controlled_buffer_6
  D_Flip_Flop d_ff_7 (.D(multiplexer_7_out), .clk(reg_clk), .Q(reg_int_out[1]));  // open: Qn, preset, reset
  Multiplexer multiplexer_8 (.in0(reg_int_out[0]), .in1(reg_in[0]), .out(multiplexer_8_out), .sel(reg_in_en));
  D_Flip_Flop d_ff_8 (.D(multiplexer_8_out), .clk(reg_clk), .Q(reg_int_out[0]));  // open: Qn, preset, reset
  assign reg_out[1] = reg_out_en ? reg_int_out[1] : 1'bz;  // Controlled_Buffer controlled_buffer_7
  assign reg_out[0] = reg_out_en ? reg_int_out[0] : 1'bz;  // Controlled_Buffer controlled_buffer_8

  // Notes on the sheet:
  //   input control
  //   output control
  //   clock
  //   input
  //   output
  //   internal output
endmodule

module alu_8bit (
  input  [7:0] alu_in_1,
  input  alu_out_en,
  input  [7:0] alu_in_2,
  input  [2:0] alu_select,
  output [7:0] xor_result,
  output [7:0] or_result,
  output [7:0] and_result,
  output [7:0] alu_out,
  output alu_carry_out
);

  wire adder_2_cout, adder_3_cout, adder_4_cout, adder_5_cout, adder_6_cout, adder_7_cout, adder_8_cout,
       and_1_out, not_1_out, not_2_out, xor_1_out, xor_2_out, xor_3_out, xor_5_out, xor_6_out, xor_7_out,
       xor_8_out, xor_9_out;
  wire [7:0] adder_8_out, multiplexer_1_out;

  not not_1 (not_1_out, alu_select[1]);
  not not_2 (not_2_out, alu_select[2]);
  and and_1 (and_1_out, alu_select[0], not_1_out, not_2_out);
  xor xor_1 (xor_1_out, alu_in_2[7], and_1_out);
  Adder #(.width(1)) adder_1 (
    .a(alu_in_1[7]), .b(xor_1_out), .out(adder_8_out[7]), .cin(adder_2_cout), .cout(alu_carry_out));
  xor xor_2 (xor_2_out, alu_in_2[6], and_1_out);
  Adder #(.width(1)) adder_2 (
    .a(alu_in_1[6]), .b(xor_2_out), .out(adder_8_out[6]), .cin(adder_3_cout), .cout(adder_2_cout));
  xor xor_3 (xor_3_out, alu_in_2[5], and_1_out);
  assign xor_result = alu_in_1 ^ alu_in_2;  // XOR_Gate xor_4, 8 bits wide
  assign or_result = alu_in_1 | alu_in_2;  // OR_Gate or_1, 8 bits wide
  assign and_result = alu_in_1 & alu_in_2;  // AND_Gate and_2, 8 bits wide
  Adder #(.width(1)) adder_3 (
    .a(alu_in_1[5]), .b(xor_3_out), .out(adder_8_out[5]), .cin(adder_4_cout), .cout(adder_3_cout));
  xor xor_5 (xor_5_out, alu_in_2[4], and_1_out);
  Adder #(.width(1)) adder_4 (
    .a(alu_in_1[4]), .b(xor_5_out), .out(adder_8_out[4]), .cin(adder_5_cout), .cout(adder_4_cout));
  xor xor_6 (xor_6_out, alu_in_2[3], and_1_out);
  Adder #(.width(1)) adder_5 (
    .a(alu_in_1[3]), .b(xor_6_out), .out(adder_8_out[3]), .cin(adder_6_cout), .cout(adder_5_cout));
  xor xor_7 (xor_7_out, alu_in_2[2], and_1_out);
  Adder #(.width(1)) adder_6 (
    .a(alu_in_1[2]), .b(xor_7_out), .out(adder_8_out[2]), .cin(adder_7_cout), .cout(adder_6_cout));
  xor xor_8 (xor_8_out, alu_in_2[1], and_1_out);
  Adder #(.width(1)) adder_7 (
    .a(alu_in_1[1]), .b(xor_8_out), .out(adder_8_out[1]), .cin(adder_8_cout), .cout(adder_7_cout));
  xor xor_9 (xor_9_out, alu_in_2[0], and_1_out);
  Adder #(.width(1)) adder_8 (
    .a(alu_in_1[0]), .b(xor_9_out), .out(adder_8_out[0]), .cin(and_1_out), .cout(adder_8_cout));
  Multiplexer #(.select(3), .width(8)) multiplexer_1 (
    .in0(adder_8_out), .in1(adder_8_out), .in2(and_result), .in3(or_result), .in4(xor_result),
    .in5({8{1'b0}}), .in6({8{1'b0}}), .in7({8{1'b0}}), .out(multiplexer_1_out), .sel(alu_select));
  assign alu_out = alu_out_en ? multiplexer_1_out : 8'bz;  // Controlled_Buffer controlled_buffer_1

  // Notes on the sheet:
  //   input 1
  //   carry output
  //   SUB control
  //   input 2
  //   output control
  //   ALU output
endmodule

module pc_4bit_ripple_lab (
  input  pc_en,
  input  pc_clk,
  input  pc_reset,
  input  pc_out_en,
  output [3:0] pc_value,
  output [3:0] pc_out
);

  wire j_k_ff_2_qn, j_k_ff_3_qn, j_k_ff_4_qn;

  J_K_Flip_Flop j_k_ff_1 (
    .J(pc_en), .K(pc_en), .clk(j_k_ff_2_qn), .Q(pc_value[3]), .reset(pc_reset));  // open: Qn, preset
  J_K_Flip_Flop j_k_ff_2 (
    .J(pc_en), .K(pc_en), .clk(j_k_ff_3_qn), .Q(pc_value[2]), .Qn(j_k_ff_2_qn), .reset(pc_reset));  // open: preset
  J_K_Flip_Flop j_k_ff_3 (
    .J(pc_en), .K(pc_en), .clk(j_k_ff_4_qn), .Q(pc_value[1]), .Qn(j_k_ff_3_qn), .reset(pc_reset));  // open: preset
  J_K_Flip_Flop j_k_ff_4 (
    .J(pc_en), .K(pc_en), .clk(pc_clk), .Q(pc_value[0]), .Qn(j_k_ff_4_qn), .reset(pc_reset));  // open: preset
  assign pc_out = pc_out_en ? pc_value : 4'bz;  // Controlled_Buffer controlled_buffer_1

  // Notes on the sheet:
  //   clock
  //   reset
  //   count control
  //   output control
  //   counter output
endmodule

module decoder_4x16 (
  input  [3:0] dec_sel,
  output [15:0] dec_out
);

  wire not_1_out, not_2_out, not_3_out, not_4_out;

  not not_1 (not_1_out, dec_sel[3]);
  not not_2 (not_2_out, dec_sel[2]);
  not not_3 (not_3_out, dec_sel[1]);
  not not_4 (not_4_out, dec_sel[0]);
  and and_1 (dec_out[0], not_4_out, not_3_out, not_2_out, not_1_out);
  and and_2 (dec_out[1], dec_sel[0], not_3_out, not_2_out, not_1_out);
  and and_3 (dec_out[2], not_4_out, dec_sel[1], not_2_out, not_1_out);
  and and_4 (dec_out[3], dec_sel[0], dec_sel[1], not_2_out, not_1_out);
  and and_5 (dec_out[4], not_4_out, not_3_out, dec_sel[2], not_1_out);
  and and_6 (dec_out[5], dec_sel[0], not_3_out, dec_sel[2], not_1_out);
  and and_7 (dec_out[6], not_4_out, dec_sel[1], dec_sel[2], not_1_out);
  and and_8 (dec_out[7], dec_sel[0], dec_sel[1], dec_sel[2], not_1_out);
  and and_9 (dec_out[8], not_4_out, not_3_out, not_2_out, dec_sel[3]);
  and and_10 (dec_out[9], dec_sel[0], not_3_out, not_2_out, dec_sel[3]);
  and and_11 (dec_out[10], not_4_out, dec_sel[1], not_2_out, dec_sel[3]);
  and and_12 (dec_out[11], dec_sel[0], dec_sel[1], not_2_out, dec_sel[3]);
  and and_13 (dec_out[12], not_4_out, not_3_out, dec_sel[2], dec_sel[3]);
  and and_14 (dec_out[13], dec_sel[0], not_3_out, dec_sel[2], dec_sel[3]);
  and and_15 (dec_out[14], not_4_out, dec_sel[1], dec_sel[2], dec_sel[3]);
  and and_16 (dec_out[15], dec_sel[0], dec_sel[1], dec_sel[2], dec_sel[3]);
endmodule

module ram_cell_8bit (
  input  [7:0] data_in,
  input  wr_en,
  input  clk,
  input  cs,
  input  rd_en,
  output [7:0] memory_content,
  output [7:0] data_out
);

  wire and_1_out, and_2_out;

  and and_1 (and_1_out, wr_en, cs);
  and and_2 (and_2_out, cs, rd_en);
  register_8bit register_8bit_1 (
    .reg_in(data_in), .reg_in_en(and_1_out), .reg_clk(clk), .reg_out_en(and_2_out),
    .reg_int_out(memory_content), .reg_out(data_out));
endmodule

module ram_16x8 (
  input  sram_rd,
  input  sram_wr,
  input  [7:0] sram_d_in,
  input  [7:0] mar_d_in,
  input  mar_in_en,
  input  sram_clk,
  output [7:0] sram_d_out,
  output [7:0] out_8,
  output [7:0] out_9,
  output [7:0] out_10,
  output [7:0] out_11,
  output [7:0] out_12,
  output [7:0] out_13,
  output [7:0] out_14,
  output [7:0] out_15,
  output [7:0] out_16,
  output [7:0] out_17,
  output [7:0] out_18,
  output [7:0] out_19,
  output [7:0] out_20,
  output [7:0] out_21,
  output [7:0] out_22,
  output [7:0] out_23
);

  wire [7:0] controlled_buffer_1_out, register_8bit_1_reg_int_out;
  wire [15:0] decoder_4x16_1_dec_out;

  decoder_4x16 decoder_4x16_1 (.dec_sel(register_8bit_1_reg_int_out[3:0]), .dec_out(decoder_4x16_1_dec_out));
  register_8bit register_8bit_1 (
    .reg_in(mar_d_in), .reg_in_en(mar_in_en), .reg_clk(sram_clk), .reg_int_out(register_8bit_1_reg_int_out));  // open: reg_out_en, reg_out
  assign controlled_buffer_1_out = sram_wr ? sram_d_in : 8'bz;  // Controlled_Buffer controlled_buffer_1
  ram_cell_8bit ram_cell_8bit_1 (
    .data_in(controlled_buffer_1_out), .wr_en(sram_wr), .clk(sram_clk), .cs(decoder_4x16_1_dec_out[0]),
    .rd_en(sram_rd), .memory_content(out_8), .data_out(controlled_buffer_1_out));
  ram_cell_8bit ram_cell_8bit_2 (
    .data_in(controlled_buffer_1_out), .wr_en(sram_wr), .clk(sram_clk), .cs(decoder_4x16_1_dec_out[1]),
    .rd_en(sram_rd), .memory_content(out_9), .data_out(controlled_buffer_1_out));
  ram_cell_8bit ram_cell_8bit_3 (
    .data_in(controlled_buffer_1_out), .wr_en(sram_wr), .clk(sram_clk), .cs(decoder_4x16_1_dec_out[2]),
    .rd_en(sram_rd), .memory_content(out_10), .data_out(controlled_buffer_1_out));
  ram_cell_8bit ram_cell_8bit_4 (
    .data_in(controlled_buffer_1_out), .wr_en(sram_wr), .clk(sram_clk), .cs(decoder_4x16_1_dec_out[3]),
    .rd_en(sram_rd), .memory_content(out_11), .data_out(controlled_buffer_1_out));
  ram_cell_8bit ram_cell_8bit_5 (
    .data_in(controlled_buffer_1_out), .wr_en(sram_wr), .clk(sram_clk), .cs(decoder_4x16_1_dec_out[4]),
    .rd_en(sram_rd), .memory_content(out_12), .data_out(controlled_buffer_1_out));
  ram_cell_8bit ram_cell_8bit_6 (
    .data_in(controlled_buffer_1_out), .wr_en(sram_wr), .clk(sram_clk), .cs(decoder_4x16_1_dec_out[5]),
    .rd_en(sram_rd), .memory_content(out_13), .data_out(controlled_buffer_1_out));
  ram_cell_8bit ram_cell_8bit_7 (
    .data_in(controlled_buffer_1_out), .wr_en(sram_wr), .clk(sram_clk), .cs(decoder_4x16_1_dec_out[6]),
    .rd_en(sram_rd), .memory_content(out_14), .data_out(controlled_buffer_1_out));
  ram_cell_8bit ram_cell_8bit_8 (
    .data_in(controlled_buffer_1_out), .wr_en(sram_wr), .clk(sram_clk), .cs(decoder_4x16_1_dec_out[7]),
    .rd_en(sram_rd), .memory_content(out_15), .data_out(controlled_buffer_1_out));
  ram_cell_8bit ram_cell_8bit_9 (
    .data_in(controlled_buffer_1_out), .wr_en(sram_wr), .clk(sram_clk), .cs(decoder_4x16_1_dec_out[8]),
    .rd_en(sram_rd), .memory_content(out_16), .data_out(controlled_buffer_1_out));
  ram_cell_8bit ram_cell_8bit_10 (
    .data_in(controlled_buffer_1_out), .wr_en(sram_wr), .clk(sram_clk), .cs(decoder_4x16_1_dec_out[9]),
    .rd_en(sram_rd), .memory_content(out_17), .data_out(controlled_buffer_1_out));
  ram_cell_8bit ram_cell_8bit_11 (
    .data_in(controlled_buffer_1_out), .wr_en(sram_wr), .clk(sram_clk), .cs(decoder_4x16_1_dec_out[10]),
    .rd_en(sram_rd), .memory_content(out_18), .data_out(controlled_buffer_1_out));
  ram_cell_8bit ram_cell_8bit_12 (
    .data_in(controlled_buffer_1_out), .wr_en(sram_wr), .clk(sram_clk), .cs(decoder_4x16_1_dec_out[11]),
    .rd_en(sram_rd), .memory_content(out_19), .data_out(controlled_buffer_1_out));
  ram_cell_8bit ram_cell_8bit_13 (
    .data_in(controlled_buffer_1_out), .wr_en(sram_wr), .clk(sram_clk), .cs(decoder_4x16_1_dec_out[12]),
    .rd_en(sram_rd), .memory_content(out_20), .data_out(controlled_buffer_1_out));
  ram_cell_8bit ram_cell_8bit_14 (
    .data_in(controlled_buffer_1_out), .wr_en(sram_wr), .clk(sram_clk), .cs(decoder_4x16_1_dec_out[13]),
    .rd_en(sram_rd), .memory_content(out_21), .data_out(controlled_buffer_1_out));
  ram_cell_8bit ram_cell_8bit_15 (
    .data_in(controlled_buffer_1_out), .wr_en(sram_wr), .clk(sram_clk), .cs(decoder_4x16_1_dec_out[14]),
    .rd_en(sram_rd), .memory_content(out_22), .data_out(controlled_buffer_1_out));
  ram_cell_8bit ram_cell_8bit_16 (
    .data_in(controlled_buffer_1_out), .wr_en(sram_wr), .clk(sram_clk), .cs(decoder_4x16_1_dec_out[15]),
    .rd_en(sram_rd), .memory_content(out_23), .data_out(controlled_buffer_1_out));
  assign sram_d_out = sram_rd ? controlled_buffer_1_out : 8'bz;  // Controlled_Buffer controlled_buffer_2
endmodule

module instruction_register (
  input  operand_out_en,
  input  [7:0] ir_in,
  input  ir_in_en,
  input  clk,
  output [7:0] operand_bus_out,
  output [3:0] operand_out,
  output [3:0] opcode_out
);

  wire [7:0] bit_extender_1_out;

  register_8bit register_8bit_1 (
    .reg_in(ir_in), .reg_in_en(ir_in_en), .reg_clk(clk), .reg_int_out({opcode_out, operand_out}));  // open: reg_out_en, reg_out
  assign bit_extender_1_out = {{4{1'b0}}, operand_out};  // Bit_Extender bit_extender_1
  assign operand_bus_out = operand_out_en ? bit_extender_1_out : 8'bz;  // Controlled_Buffer controlled_buffer_1
endmodule

module sap1_manual_top (
  input  in_1,
  input  in_2,
  input  in_3,
  input  in_4,
  input  in_5,
  input  in_6,
  input  in_7,
  input  in_8,
  input  in_9,
  input  in_10,
  input  in_11,
  input  in_12,
  input  in_13,
  input  in_14,
  input  in_15,
  input  in_16,
  input  [7:0] in_17,
  output [3:0] out_18,
  output [7:0] out_19,
  output [7:0] out_20,
  output [7:0] out_21,
  output [7:0] out_22,
  output [7:0] out_23,
  output [7:0] out_24,
  output [7:0] out_25,
  output [7:0] out_26,
  output [7:0] out_27,
  output [7:0] out_28,
  output [7:0] out_29,
  output [7:0] out_30,
  output [7:0] out_31,
  output [7:0] out_32,
  output [7:0] out_33,
  output [7:0] out_34,
  output [7:0] out_35,
  output [7:0] out_36,
  output [3:0] out_37,
  output [3:0] out_38,
  output [7:0] out_39
);

  wire [7:4] instruction_register_1_operand_bus_out;

  pc_4bit_ripple_lab pc_4bit_ripple_lab_1 (
    .pc_en(in_12), .pc_clk(in_15), .pc_reset(in_14), .pc_out_en(in_13), .pc_value(out_18), .pc_out(out_37));
  ram_16x8 ram_16x8_1 (
    .sram_rd(in_8), .sram_wr(in_9), .sram_d_in({out_39[7:4], out_37}), .mar_d_in({out_39[7:4], out_37}),
    .mar_in_en(in_7), .sram_clk(in_15), .sram_d_out({out_39[7:4], out_37}), .out_8(out_20), .out_9(out_21),
    .out_10(out_22), .out_11(out_23), .out_12(out_24), .out_13(out_25), .out_14(out_26), .out_15(out_27),
    .out_16(out_28), .out_17(out_30), .out_18(out_31), .out_19(out_32), .out_20(out_33), .out_21(out_34),
    .out_22(out_35), .out_23(out_36));
  assign {out_39[7:4], out_37} = in_16 ? in_17 : 8'bz;  // Controlled_Buffer controlled_buffer_1
  register_8bit register_8bit_1 (
    .reg_in({out_39[7:4], out_37}), .reg_in_en(in_1), .reg_clk(in_15), .reg_out_en(in_2),
    .reg_int_out(out_19), .reg_out({out_39[7:4], out_37}));
  register_8bit register_8bit_2 (
    .reg_in({out_39[7:4], out_37}), .reg_in_en(in_3), .reg_clk(in_15), .reg_out_en(in_4),
    .reg_int_out(out_29), .reg_out({out_39[7:4], out_37}));
  // alu_8bit alu_8bit_1: pin names not known; wires that end beside it: out_19, in_5, in_6, out_29, {out_39[7:4], out_37}
  instruction_register instruction_register_1 (
    .operand_out_en(in_11), .ir_in({out_39[7:4], out_37}), .ir_in_en(in_10), .clk(in_15),
    .operand_bus_out({instruction_register_1_operand_bus_out, out_37}), .operand_out(out_38));  // open: opcode_out
  // Pins of 4 and 8 bits meet at {instruction_register_1_operand_bus_out, out_37}

  assign out_39[3:0] = out_37;

  // Other names for the same wires on the sheet: a_in = in_1; a_out = in_2; alu_out = in_5; alu_sub = in_6;
  //   b_in = in_3; b_out = in_4; clk = in_15; debug = in_16; debug_data[7:0] = in_17; ins_reg_in_en = in_10;
  //   ins_reg_out_en = in_11; mar_in_en = in_7; pc_en = in_12; pc_out = in_13; pc_reset = in_14; sram_rd = in_8;
  //   sram_wr = in_9
endmodule

module sap1_final_top (
  input  in_1,
  input  in_2,
  input  in_3,
  input  in_4,
  input  in_5,
  input  [7:0] in_6,
  input  in_7,
  input  in_8,
  input  in_9,
  input  in_10,
  output [3:0] out_11,
  output [7:0] out_12,
  output [7:0] out_13,
  output [7:0] out_14,
  output [7:0] out_15,
  output [7:0] out_16,
  output [7:0] out_17,
  output [7:0] out_18,
  output [7:0] out_19,
  output [7:0] out_20,
  output [7:0] out_21,
  output [7:0] out_22,
  output [7:0] out_23,
  output [7:0] out_24,
  output [7:0] out_25,
  output C,
  output [7:0] out_27,
  output [7:0] out_28,
  output [7:0] out_29,
  output [7:0] out_30,
  output [3:0] out_31,
  output [7:0] out_32,
  output [3:0] out_33,
  output [2:0] out_34
);

  wire a_in, a_out, alu_8bit_1_alu_carry_out, alu_out_en, and_1_out, b_in, carry_load, const_zero_out,
       control_sequencer_1_mar_in, control_sequencer_1_ram_in, control_sequencer_1_ram_out, CPU_CLK,
       DEBUG_MAR_IN, DEBUG_RAM_WR, HLT, ins_reg_in_en, ins_reg_out_en, loader_bus_en, loader_done,
       loader_mar_in, loader_phase, loader_ram_wr, mar_in_en, multiplexer_1_out, pc_in_en, pc_inc, pc_out_en,
       pc_reset, rotate_data_in, rotate_mode_in, rotate_out_en, shift_data_in, shift_mode_in, shift_out_en,
       sram_rd, sram_wr, T0, T1, T2, T3, T4, T5, TIMING_RESET, zero_flag;
  wire [2:0] alu_select;
  wire [3:0] loader_addr;
  wire [7:0] alu_8bit_1_and_result, alu_8bit_1_or_result, alu_8bit_1_xor_result, loader_data,
       multiplexer_2_out;

  // Probe on CPU_CLK
  // Probe on TIMING_RESET
  pc_4bit_loadable pc_4bit_loadable_1 (
    .pc_inc(pc_inc), .pc_in(out_32[3:0]), .pc_in_en(pc_in_en), .pc_reset(pc_reset), .pc_clk(CPU_CLK),
    .pc_out_en(pc_out_en), .pc_value(out_11), .pc_out(out_32[3:0]));
  ram_16x8 ram_16x8_1 (
    .sram_rd(sram_rd), .sram_wr(sram_wr), .sram_d_in(out_32), .mar_d_in(out_32), .mar_in_en(mar_in_en),
    .sram_clk(CPU_CLK), .sram_d_out(out_32), .out_8(out_13), .out_9(out_14), .out_10(out_15),
    .out_11(out_16), .out_12(out_17), .out_13(out_18), .out_14(out_19), .out_15(out_20), .out_16(out_21),
    .out_17(out_23), .out_18(out_24), .out_19(out_25), .out_20(out_27), .out_21(out_28), .out_22(out_29),
    .out_23(out_30));
  ring_counter ring_counter_1 (
    .clk(CPU_CLK), .ring_reset(TIMING_RESET), .ring_value(out_34), .T0(T0), .T1(T1), .T2(T2), .T3(T3),
    .T4(T4), .T5(T5));  // open: out_3
  and and_1 (and_1_out, in_4, multiplexer_1_out);
  assign out_32 = and_1_out ? multiplexer_2_out : 8'bz;  // Controlled_Buffer controlled_buffer_1
  Multiplexer multiplexer_1 (.in0(in_7), .in1(loader_bus_en), .out(multiplexer_1_out), .sel(in_3));
  Multiplexer #(.width(8)) multiplexer_2 (.in0(in_6), .in1(loader_data), .out(multiplexer_2_out), .sel(in_3));
  // Probe on out_32
  assign out_32 = const_zero_out ? {8{1'b0}} : 8'bz;  // Controlled_Buffer controlled_buffer_2
  // Probe on {8{1'b0}}
  // Probe on alu_select
  register_8bit register_8bit_1 (
    .reg_in(out_32), .reg_in_en(a_in), .reg_clk(CPU_CLK), .reg_out_en(a_out), .reg_int_out(out_12),
    .reg_out(out_32));
  register_8bit register_8bit_2 (
    .reg_in(out_32), .reg_in_en(b_in), .reg_clk(CPU_CLK), .reg_out_en(1'b0), .reg_int_out(out_22));  // open: reg_out
  // Probe on zero_flag
  zero_detector zero_detector_1 (.A(out_12), .Z(zero_flag));
  alu_8bit alu_8bit_1 (
    .alu_in_1(out_12), .alu_out_en(alu_out_en), .alu_in_2(out_22), .alu_select(alu_select),
    .xor_result(alu_8bit_1_xor_result), .or_result(alu_8bit_1_or_result), .and_result(alu_8bit_1_and_result),
    .alu_out(out_32), .alu_carry_out(alu_8bit_1_alu_carry_out));
  instruction_register instruction_register_1 (
    .operand_out_en(ins_reg_out_en), .ir_in(out_32), .ir_in_en(ins_reg_in_en), .clk(CPU_CLK),
    .operand_bus_out(out_32), .operand_out(out_31), .opcode_out(out_33));
  ring_rotator_8bit ring_rotator_8bit_1 (
    .rotate_data(out_32), .rotate_data_in(rotate_data_in), .rotate_out_en(rotate_out_en), .clk(CPU_CLK),
    .rotate_mode(out_32[3:0]), .rotate_mode_in(rotate_mode_in), .rotate_result(out_32));
  // Probe on alu_8bit_1_xor_result
  // Probe on alu_8bit_1_or_result
  // Probe on alu_8bit_1_and_result
  carry_register_1bit carry_register_1bit_1 (
    .carry_in(alu_8bit_1_alu_carry_out), .carry_load(carry_load), .carry_reset(in_2), .clk(CPU_CLK),
    .carry_out(C));
  Multiplexer multiplexer_3 (.in0(in_9), .in1(loader_ram_wr), .out(DEBUG_RAM_WR), .sel(in_3));
  Multiplexer multiplexer_4 (.in0(in_8), .in1(loader_mar_in), .out(DEBUG_MAR_IN), .sel(in_3));
  ram_loader_8bit ram_loader_8bit_1 (
    .loader_clk(in_1), .load_mode(in_3), .load_reset(in_5), .loader_bus_data(loader_data),
    .loader_bus_en(loader_bus_en), .loader_mar_in(loader_mar_in), .loader_ram_wr(loader_ram_wr),
    .loader_done(loader_done), .loader_address(loader_addr), .loader_phase(loader_phase));
  // Probe on out_32
  barrel_shifter_8bit barrel_shifter_8bit_1 (
    .shift_data(out_32), .shift_data_in(shift_data_in), .shift_out_en(shift_out_en), .clk(CPU_CLK),
    .shift_mode(out_32[3:0]), .shift_mode_in(shift_mode_in), .shift_result(out_32));
  clock_control clock_control_1 (.CLK_RAW(in_1), .HLT(HLT), .CPU_CLK(CPU_CLK));
  control_sequencer control_sequencer_1 (
    .T0(T0), .T1(T1), .T2(T2), .T3(T3), .T4(T4), .T5(T5), .C(C), .Z(zero_flag), .debug(in_4), .reset(in_2),
    .opcode(out_33), .CONST_ZERO_OUT(const_zero_out), .SHIFT_MODE_IN(shift_mode_in),
    .MAR_IN(control_sequencer_1_mar_in), .A_IN(a_in), .PC_OUT(pc_out_en), .TIMING_RESET(TIMING_RESET),
    .SHIFT_DATA_IN(shift_data_in), .RAM_OUT(control_sequencer_1_ram_out), .A_OUT(a_out), .HLT(HLT),
    .PC_IN(pc_in_en), .SHIFT_OUT(shift_out_en), .RAM_IN(control_sequencer_1_ram_in), .B_IN(b_in),
    .ROTATE_MODE_IN(rotate_mode_in), .PC_INC(pc_inc), .IR_IN(ins_reg_in_en), .ALU_OUT(alu_out_en),
    .ROTATE_DATA_IN(rotate_data_in), .PC_RESET(pc_reset), .OPERAND_OUT(ins_reg_out_en),
    .ALU_SELECT(alu_select), .ROTATE_OUT(rotate_out_en), .CARRY_LOAD(carry_load));
  Multiplexer multiplexer_5 (.in0(control_sequencer_1_mar_in), .in1(DEBUG_MAR_IN), .out(mar_in_en), .sel(in_4));
  Multiplexer multiplexer_6 (.in0(control_sequencer_1_ram_out), .in1(in_10), .out(sram_rd), .sel(in_4));
  Multiplexer multiplexer_7 (.in0(control_sequencer_1_ram_in), .in1(DEBUG_RAM_WR), .out(sram_wr), .sel(in_4));
  // Probe on out_11
  // Probe on out_32
  // Probe on out_12
  // Probe on out_22
  // Probe on C
  // Probe on zero_flag
  // Probe on HLT
  // Probe on loader_data
  // Probe on loader_bus_en
  // Probe on loader_mar_in
  // Probe on loader_ram_wr
  // Probe on loader_addr
  // Probe on loader_phase
  // Probe on loader_done
  LED led_1 (.in(loader_done));

  // Other names for the same wires on the sheet: BUS_Value[7:0] = out_32; CARRY_OUT = C; CLK_RAW = in_1; debug = in_4;
  //   debug_data[7:0] = in_6; DEBUG_DATA_EN = in_7; LOAD_MODE = in_3; LOAD_RESET = in_5; MAN_MAR_IN = in_8;
  //   MAN_RAM_RD = in_10; MAN_RAM_WR = in_9; opcode_out[3:0] = out_33; pc_value[3:0] = out_11;
  //   REGISTER_A[7:0] = out_12; REGISTER_B[7:0] = out_22; reset = in_2

  // Notes on the sheet:
  //   inputs
  //   OUTPUTS
endmodule

module pc_4bit_loadable (
  input  pc_inc,
  input  [3:0] pc_in,
  input  pc_in_en,
  input  pc_reset,
  input  pc_clk,
  input  pc_out_en,
  output [3:0] pc_value,
  output [3:0] pc_out
);

  wire AND1_out, AND2_out, AND3_out, multiplexer_1_out, multiplexer_2_out, multiplexer_3_out,
       multiplexer_4_out, multiplexer_5_out, multiplexer_6_out, multiplexer_7_out, multiplexer_8_out,
       not_1_out, not_2_out, not_3_out, not_4_out;

  Multiplexer multiplexer_1 (.in0(AND3_out), .in1(pc_in[3]), .out(multiplexer_1_out), .sel(pc_in_en));
  Multiplexer multiplexer_2 (.in0(AND3_out), .in1(not_1_out), .out(multiplexer_2_out), .sel(pc_in_en));
  J_K_Flip_Flop MSB (
    .J(multiplexer_1_out), .K(multiplexer_2_out), .clk(pc_clk), .Q(pc_value[3]), .reset(pc_reset));  // open: Qn, preset
  and AND3 (AND3_out, pc_inc, pc_value[2], pc_value[1], pc_value[0]);
  not not_1 (not_1_out, pc_in[3]);
  and AND2 (AND2_out, pc_inc, pc_value[1], pc_value[0]);
  Multiplexer multiplexer_3 (.in0(AND2_out), .in1(pc_in[2]), .out(multiplexer_3_out), .sel(pc_in_en));
  Multiplexer multiplexer_4 (.in0(AND2_out), .in1(not_2_out), .out(multiplexer_4_out), .sel(pc_in_en));
  J_K_Flip_Flop bit2 (
    .J(multiplexer_3_out), .K(multiplexer_4_out), .clk(pc_clk), .Q(pc_value[2]), .reset(pc_reset));  // open: Qn, preset
  not not_2 (not_2_out, pc_in[2]);
  and AND1 (AND1_out, pc_inc, pc_value[0]);
  Multiplexer multiplexer_5 (.in0(AND1_out), .in1(pc_in[1]), .out(multiplexer_5_out), .sel(pc_in_en));
  Multiplexer multiplexer_6 (.in0(AND1_out), .in1(not_3_out), .out(multiplexer_6_out), .sel(pc_in_en));
  not not_3 (not_3_out, pc_in[1]);
  J_K_Flip_Flop bit1 (
    .J(multiplexer_5_out), .K(multiplexer_6_out), .clk(pc_clk), .Q(pc_value[1]), .reset(pc_reset));  // open: Qn, preset
  Multiplexer multiplexer_7 (.in0(pc_inc), .in1(not_4_out), .out(multiplexer_7_out), .sel(pc_in_en));
  Multiplexer multiplexer_8 (.in0(pc_inc), .in1(pc_in[0]), .out(multiplexer_8_out), .sel(pc_in_en));
  not not_4 (not_4_out, pc_in[0]);
  J_K_Flip_Flop LSB (
    .J(multiplexer_8_out), .K(multiplexer_7_out), .clk(pc_clk), .Q(pc_value[0]), .reset(pc_reset));  // open: Qn, preset
  assign pc_out = pc_out_en ? pc_value : 4'bz;  // Controlled_Buffer controlled_buffer_1
endmodule

module carry_register_1bit (
  input  carry_in,
  input  carry_load,
  input  carry_reset,
  input  clk,
  output carry_out
);

  wire multiplexer_1_out, multiplexer_2_out;

  Multiplexer multiplexer_1 (.in0(carry_out), .in1(carry_in), .out(multiplexer_1_out), .sel(carry_load));
  Multiplexer multiplexer_2 (.in0(multiplexer_1_out), .in1(1'b0), .out(multiplexer_2_out), .sel(carry_reset));
  D_Flip_Flop Carry_FF (.D(multiplexer_2_out), .clk(clk), .Q(carry_out));  // open: Qn, preset, reset

  // Notes on the sheet:
  //   LOAD MUX
  //   RESET MUX
endmodule

module zero_detector (
  input  [7:0] A,
  output Z
);

  nor nor_1 (Z, A[7], A[6], A[5], A[4], A[3], A[2], A[1], A[0]);
endmodule

module barrel_shifter_8bit (
  input  [7:0] shift_data,
  input  shift_data_in,
  input  shift_out_en,
  input  clk,
  input  [3:0] shift_mode,
  input  shift_mode_in,
  output [7:0] shift_result
);

  wire multiplexer_2_out, multiplexer_3_out, multiplexer_4_out, multiplexer_5_out, multiplexer_6_out,
       multiplexer_7_out, multiplexer_8_out, multiplexer_9_out, multiplexer_10_out, multiplexer_11_out,
       multiplexer_12_out, multiplexer_13_out, multiplexer_14_out, multiplexer_15_out, multiplexer_16_out,
       multiplexer_17_out;
  wire [7:0] multiplexer_1_out, multiplexer_25_out, multiplexer_26_out, register_8bit_1_reg_int_out,
       register_8bit_2_reg_int_out;

  register_8bit register_8bit_1 (
    .reg_in(shift_data), .reg_in_en(shift_data_in), .reg_clk(clk), .reg_out_en(1'b0),
    .reg_int_out(register_8bit_1_reg_int_out));  // open: reg_out
  register_8bit register_8bit_2 (
    .reg_in({4'b0000, shift_mode}), .reg_in_en(shift_mode_in), .reg_clk(clk), .reg_out_en(1'b0),
    .reg_int_out(register_8bit_2_reg_int_out));  // open: reg_out
  Multiplexer #(.width(8)) multiplexer_1 (
    .in0({register_8bit_1_reg_int_out[0], register_8bit_1_reg_int_out[1], register_8bit_1_reg_int_out[2], register_8bit_1_reg_int_out[3], register_8bit_1_reg_int_out[4], register_8bit_1_reg_int_out[5], register_8bit_1_reg_int_out[6], register_8bit_1_reg_int_out[7]}),
    .in1(register_8bit_1_reg_int_out), .out(multiplexer_1_out), .sel(register_8bit_2_reg_int_out[3]));
  Multiplexer multiplexer_2 (
    .in0(multiplexer_1_out[0]), .in1(multiplexer_1_out[1]), .out(multiplexer_2_out),
    .sel(register_8bit_2_reg_int_out[0]));
  Multiplexer multiplexer_3 (
    .in0(multiplexer_1_out[1]), .in1(multiplexer_1_out[2]), .out(multiplexer_3_out),
    .sel(register_8bit_2_reg_int_out[0]));
  Multiplexer multiplexer_4 (
    .in0(multiplexer_1_out[2]), .in1(multiplexer_1_out[3]), .out(multiplexer_4_out),
    .sel(register_8bit_2_reg_int_out[0]));
  Multiplexer multiplexer_5 (
    .in0(multiplexer_1_out[3]), .in1(multiplexer_1_out[4]), .out(multiplexer_5_out),
    .sel(register_8bit_2_reg_int_out[0]));
  Multiplexer multiplexer_6 (
    .in0(multiplexer_1_out[4]), .in1(multiplexer_1_out[5]), .out(multiplexer_6_out),
    .sel(register_8bit_2_reg_int_out[0]));
  Multiplexer multiplexer_7 (
    .in0(multiplexer_1_out[5]), .in1(multiplexer_1_out[6]), .out(multiplexer_7_out),
    .sel(register_8bit_2_reg_int_out[0]));
  Multiplexer multiplexer_8 (
    .in0(multiplexer_1_out[6]), .in1(multiplexer_1_out[7]), .out(multiplexer_8_out),
    .sel(register_8bit_2_reg_int_out[0]));
  Multiplexer multiplexer_9 (
    .in0(multiplexer_1_out[7]), .in1(1'b0), .out(multiplexer_9_out), .sel(register_8bit_2_reg_int_out[0]));
  Multiplexer multiplexer_10 (
    .in0(multiplexer_2_out), .in1(multiplexer_4_out), .out(multiplexer_10_out),
    .sel(register_8bit_2_reg_int_out[1]));
  Multiplexer multiplexer_11 (
    .in0(multiplexer_3_out), .in1(multiplexer_5_out), .out(multiplexer_11_out),
    .sel(register_8bit_2_reg_int_out[1]));
  Multiplexer multiplexer_12 (
    .in0(multiplexer_4_out), .in1(multiplexer_6_out), .out(multiplexer_12_out),
    .sel(register_8bit_2_reg_int_out[1]));
  Multiplexer multiplexer_13 (
    .in0(multiplexer_5_out), .in1(multiplexer_7_out), .out(multiplexer_13_out),
    .sel(register_8bit_2_reg_int_out[1]));
  Multiplexer multiplexer_14 (
    .in0(multiplexer_6_out), .in1(multiplexer_8_out), .out(multiplexer_14_out),
    .sel(register_8bit_2_reg_int_out[1]));
  Multiplexer multiplexer_15 (
    .in0(multiplexer_7_out), .in1(multiplexer_9_out), .out(multiplexer_15_out),
    .sel(register_8bit_2_reg_int_out[1]));
  Multiplexer multiplexer_16 (
    .in0(multiplexer_8_out), .in1(1'b0), .out(multiplexer_16_out), .sel(register_8bit_2_reg_int_out[1]));
  Multiplexer multiplexer_17 (
    .in0(multiplexer_9_out), .in1(1'b0), .out(multiplexer_17_out), .sel(register_8bit_2_reg_int_out[1]));
  Multiplexer multiplexer_18 (
    .in0(multiplexer_10_out), .in1(multiplexer_14_out), .out(multiplexer_25_out[0]),
    .sel(register_8bit_2_reg_int_out[2]));
  Multiplexer multiplexer_19 (
    .in0(multiplexer_11_out), .in1(multiplexer_15_out), .out(multiplexer_25_out[1]),
    .sel(register_8bit_2_reg_int_out[2]));
  Multiplexer multiplexer_20 (
    .in0(multiplexer_12_out), .in1(multiplexer_16_out), .out(multiplexer_25_out[2]),
    .sel(register_8bit_2_reg_int_out[2]));
  Multiplexer multiplexer_21 (
    .in0(multiplexer_13_out), .in1(multiplexer_17_out), .out(multiplexer_25_out[3]),
    .sel(register_8bit_2_reg_int_out[2]));
  Multiplexer multiplexer_22 (
    .in0(multiplexer_14_out), .in1(1'b0), .out(multiplexer_25_out[4]), .sel(register_8bit_2_reg_int_out[2]));
  Multiplexer multiplexer_23 (
    .in0(multiplexer_15_out), .in1(1'b0), .out(multiplexer_25_out[5]), .sel(register_8bit_2_reg_int_out[2]));
  Multiplexer multiplexer_24 (
    .in0(multiplexer_16_out), .in1(1'b0), .out(multiplexer_25_out[6]), .sel(register_8bit_2_reg_int_out[2]));
  Multiplexer multiplexer_25 (
    .in0(multiplexer_17_out), .in1(1'b0), .out(multiplexer_25_out[7]), .sel(register_8bit_2_reg_int_out[2]));
  Multiplexer #(.width(8)) multiplexer_26 (
    .in0({multiplexer_25_out[0], multiplexer_25_out[1], multiplexer_25_out[2], multiplexer_25_out[3], multiplexer_25_out[4], multiplexer_25_out[5], multiplexer_25_out[6], multiplexer_25_out[7]}),
    .in1(multiplexer_25_out), .out(multiplexer_26_out), .sel(register_8bit_2_reg_int_out[3]));
  assign shift_result = shift_out_en ? multiplexer_26_out : 8'bz;  // Controlled_Buffer controlled_buffer_1

  // Notes on the sheet:
  //   shift_data
  //   mode_register
  //   DATA_REG_OUT = S0
endmodule

module ring_rotator_8bit (
  input  [7:0] rotate_data,
  input  rotate_data_in,
  input  rotate_out_en,
  input  clk,
  input  [3:0] rotate_mode,
  input  rotate_mode_in,
  output [7:0] rotate_result
);

  wire multiplexer_2_out, multiplexer_3_out, multiplexer_4_out, multiplexer_5_out, multiplexer_6_out,
       multiplexer_7_out, multiplexer_8_out, multiplexer_9_out, multiplexer_10_out, multiplexer_11_out,
       multiplexer_12_out, multiplexer_13_out, multiplexer_14_out, multiplexer_15_out, multiplexer_16_out,
       multiplexer_17_out;
  wire [7:0] multiplexer_1_out, multiplexer_25_out, multiplexer_26_out, register_8bit_1_reg_int_out,
       register_8bit_2_reg_int_out;

  register_8bit register_8bit_1 (
    .reg_in(rotate_data), .reg_in_en(rotate_data_in), .reg_clk(clk), .reg_out_en(1'b0),
    .reg_int_out(register_8bit_1_reg_int_out));  // open: reg_out
  register_8bit register_8bit_2 (
    .reg_in({4'b0000, rotate_mode}), .reg_in_en(rotate_mode_in), .reg_clk(clk), .reg_out_en(1'b0),
    .reg_int_out(register_8bit_2_reg_int_out));  // open: reg_out
  Multiplexer #(.width(8)) multiplexer_1 (
    .in0({register_8bit_1_reg_int_out[0], register_8bit_1_reg_int_out[1], register_8bit_1_reg_int_out[2], register_8bit_1_reg_int_out[3], register_8bit_1_reg_int_out[4], register_8bit_1_reg_int_out[5], register_8bit_1_reg_int_out[6], register_8bit_1_reg_int_out[7]}),
    .in1(register_8bit_1_reg_int_out), .out(multiplexer_1_out), .sel(register_8bit_2_reg_int_out[3]));
  Multiplexer multiplexer_2 (
    .in0(multiplexer_1_out[0]), .in1(multiplexer_1_out[1]), .out(multiplexer_2_out),
    .sel(register_8bit_2_reg_int_out[0]));
  Multiplexer multiplexer_3 (
    .in0(multiplexer_1_out[1]), .in1(multiplexer_1_out[2]), .out(multiplexer_3_out),
    .sel(register_8bit_2_reg_int_out[0]));
  Multiplexer multiplexer_4 (
    .in0(multiplexer_1_out[2]), .in1(multiplexer_1_out[3]), .out(multiplexer_4_out),
    .sel(register_8bit_2_reg_int_out[0]));
  Multiplexer multiplexer_5 (
    .in0(multiplexer_1_out[3]), .in1(multiplexer_1_out[4]), .out(multiplexer_5_out),
    .sel(register_8bit_2_reg_int_out[0]));
  Multiplexer multiplexer_6 (
    .in0(multiplexer_1_out[4]), .in1(multiplexer_1_out[5]), .out(multiplexer_6_out),
    .sel(register_8bit_2_reg_int_out[0]));
  Multiplexer multiplexer_7 (
    .in0(multiplexer_1_out[5]), .in1(multiplexer_1_out[6]), .out(multiplexer_7_out),
    .sel(register_8bit_2_reg_int_out[0]));
  Multiplexer multiplexer_8 (
    .in0(multiplexer_1_out[6]), .in1(multiplexer_1_out[7]), .out(multiplexer_8_out),
    .sel(register_8bit_2_reg_int_out[0]));
  Multiplexer multiplexer_9 (
    .in0(multiplexer_1_out[7]), .in1(multiplexer_1_out[0]), .out(multiplexer_9_out),
    .sel(register_8bit_2_reg_int_out[0]));
  Multiplexer multiplexer_10 (
    .in0(multiplexer_2_out), .in1(multiplexer_4_out), .out(multiplexer_10_out),
    .sel(register_8bit_2_reg_int_out[1]));
  Multiplexer multiplexer_11 (
    .in0(multiplexer_3_out), .in1(multiplexer_5_out), .out(multiplexer_11_out),
    .sel(register_8bit_2_reg_int_out[1]));
  Multiplexer multiplexer_12 (
    .in0(multiplexer_4_out), .in1(multiplexer_6_out), .out(multiplexer_12_out),
    .sel(register_8bit_2_reg_int_out[1]));
  Multiplexer multiplexer_13 (
    .in0(multiplexer_5_out), .in1(multiplexer_7_out), .out(multiplexer_13_out),
    .sel(register_8bit_2_reg_int_out[1]));
  Multiplexer multiplexer_14 (
    .in0(multiplexer_6_out), .in1(multiplexer_8_out), .out(multiplexer_14_out),
    .sel(register_8bit_2_reg_int_out[1]));
  Multiplexer multiplexer_15 (
    .in0(multiplexer_7_out), .in1(multiplexer_9_out), .out(multiplexer_15_out),
    .sel(register_8bit_2_reg_int_out[1]));
  Multiplexer multiplexer_16 (
    .in0(multiplexer_8_out), .in1(multiplexer_2_out), .out(multiplexer_16_out),
    .sel(register_8bit_2_reg_int_out[1]));
  Multiplexer multiplexer_17 (
    .in0(multiplexer_9_out), .in1(multiplexer_3_out), .out(multiplexer_17_out),
    .sel(register_8bit_2_reg_int_out[1]));
  Multiplexer multiplexer_18 (
    .in0(multiplexer_10_out), .in1(multiplexer_14_out), .out(multiplexer_25_out[0]),
    .sel(register_8bit_2_reg_int_out[2]));
  Multiplexer multiplexer_19 (
    .in0(multiplexer_11_out), .in1(multiplexer_15_out), .out(multiplexer_25_out[1]),
    .sel(register_8bit_2_reg_int_out[2]));
  Multiplexer multiplexer_20 (
    .in0(multiplexer_12_out), .in1(multiplexer_16_out), .out(multiplexer_25_out[2]),
    .sel(register_8bit_2_reg_int_out[2]));
  Multiplexer multiplexer_21 (
    .in0(multiplexer_13_out), .in1(multiplexer_17_out), .out(multiplexer_25_out[3]),
    .sel(register_8bit_2_reg_int_out[2]));
  Multiplexer multiplexer_22 (
    .in0(multiplexer_14_out), .in1(multiplexer_10_out), .out(multiplexer_25_out[4]),
    .sel(register_8bit_2_reg_int_out[2]));
  Multiplexer multiplexer_23 (
    .in0(multiplexer_15_out), .in1(multiplexer_11_out), .out(multiplexer_25_out[5]),
    .sel(register_8bit_2_reg_int_out[2]));
  Multiplexer multiplexer_24 (
    .in0(multiplexer_16_out), .in1(multiplexer_12_out), .out(multiplexer_25_out[6]),
    .sel(register_8bit_2_reg_int_out[2]));
  Multiplexer multiplexer_25 (
    .in0(multiplexer_17_out), .in1(multiplexer_13_out), .out(multiplexer_25_out[7]),
    .sel(register_8bit_2_reg_int_out[2]));
  Multiplexer #(.width(8)) multiplexer_26 (
    .in0({multiplexer_25_out[0], multiplexer_25_out[1], multiplexer_25_out[2], multiplexer_25_out[3], multiplexer_25_out[4], multiplexer_25_out[5], multiplexer_25_out[6], multiplexer_25_out[7]}),
    .in1(multiplexer_25_out), .out(multiplexer_26_out), .sel(register_8bit_2_reg_int_out[3]));
  assign rotate_result = rotate_out_en ? multiplexer_26_out : 8'bz;  // Controlled_Buffer controlled_buffer_1

  // Notes on the sheet:
  //   shift_data
  //   mode_register
  //   DATA_REG_OUT = S0
endmodule

module ring_counter (
  input  clk,
  input  ring_reset,
  output [15:0] out_3,
  output [2:0] ring_value,
  output T0,
  output T1,
  output T2,
  output T3,
  output T4,
  output T5
);

  wire [2:0] adder_1_out, multiplexer_1_out;

  Register #(.width(3)) register_1 (.D(multiplexer_1_out), .en(1'b1), .clk(clk), .Q(ring_value), .clr(1'b0));
  Adder #(.width(3)) adder_1 (.a(ring_value), .b(3'b001), .out(adder_1_out), .cin(1'b0));  // open: cout
  Multiplexer #(.width(3)) multiplexer_1 (.in0(adder_1_out), .in1(3'b000), .out(multiplexer_1_out), .sel(ring_reset));
  decoder_4x16 decoder_4x16_1 (.dec_sel({1'b0, ring_value}), .dec_out(out_3));

  assign T0 = out_3[0];
  assign T1 = out_3[1];
  assign T2 = out_3[2];
  assign T3 = out_3[3];
  assign T4 = out_3[4];
  assign T5 = out_3[5];
endmodule

module control_sequencer (
  input  T0,
  input  T1,
  input  T2,
  input  T3,
  input  T4,
  input  T5,
  input  C,
  input  Z,
  input  debug,
  input  reset,
  input  [3:0] opcode,
  output CONST_ZERO_OUT,
  output SHIFT_MODE_IN,
  output MAR_IN,
  output A_IN,
  output PC_OUT,
  output TIMING_RESET,
  output SHIFT_DATA_IN,
  output RAM_OUT,
  output A_OUT,
  output HLT,
  output PC_IN,
  output SHIFT_OUT,
  output RAM_IN,
  output B_IN,
  output ROTATE_MODE_IN,
  output PC_INC,
  output IR_IN,
  output ALU_OUT,
  output ROTATE_DATA_IN,
  output PC_RESET,
  output OPERAND_OUT,
  output [2:0] ALU_SELECT,
  output ROTATE_OUT,
  output CARRY_LOAD
);

  wire and_10_out, and_11_out, and_12_out, and_14_out, and_27_out, and_32_out, and_33_out, and_34_out,
       and_35_out, and_37_out, AT2, AT3, AT4, AT5, AUTO_EN, C_BAR, D0, D1, D2, D3, D4, D5, D6, D7, D8, D9,
       DA, DB, DC, DD, DE, DEBUG_BAR, DF, JC_TAKEN, JNZ_TAKEN, JUMP_COND, or_1_out, or_2_out, or_3_out,
       or_4_out, or_5_out, or_6_out, or_7_out, or_8_out, or_9_out, or_10_out, or_11_out, or_12_out,
       or_13_out, or_14_out, or_15_out, or_16_out, or_18_out, or_19_out, or_23_out, RESET_BAR, Z_BAR;

  not not_1 (C_BAR, C);
  not not_2 (Z_BAR, Z);
  not not_3 (DEBUG_BAR, debug);
  not not_4 (RESET_BAR, reset);
  and and_1 (PC_OUT, T0, AUTO_EN);
  and and_2 (IR_IN, T1, AUTO_EN);
  and and_3 (AT2, T2, AUTO_EN);
  and and_4 (AT3, T3, AUTO_EN);
  and and_5 (AT4, T4, AUTO_EN);
  and and_6 (AT5, T5, AUTO_EN);
  and and_7 (AUTO_EN, DEBUG_BAR, RESET_BAR);
  decoder_4x16 decoder_4x16_1 (
    .dec_sel(opcode), .dec_out({DF, DE, DD, DC, DB, DA, D9, D8, D7, D6, D5, D4, D3, D2, D1, D0}));
  or or_1 (or_1_out, DA, DB, DC);
  or or_2 (or_2_out, DD, DE);
  and and_8 (JC_TAKEN, DB, C);
  and and_9 (JNZ_TAKEN, DC, Z_BAR);
  or or_3 (or_3_out, D0, D1, D2, D3, D4, D5);
  or or_4 (or_4_out, D6, D7, D8, D9, DD, DE);
  and and_10 (and_10_out, DB, C_BAR);
  and and_11 (and_11_out, DC, Z);
  or or_5 (or_5_out, D1, D2);
  and and_12 (and_12_out, AT3, or_5_out);
  and and_13 (RAM_IN, AT3, D3);
  or or_6 (or_6_out, D1, D2, D3, DA);
  or or_7 (or_7_out, DD, DE, JNZ_TAKEN, JC_TAKEN);
  or or_8 (or_8_out, D1, D4, D5, D6, D7, D8, D9);
  or or_9 (or_9_out, DD, DE);
  and and_14 (and_14_out, or_9_out, AT4);
  or or_10 (or_10_out, D3, DD, DE);
  and and_15 (B_IN, AT3, D2);
  or or_11 (or_11_out, D4, D5, D6, D7, D8);
  or or_12 (or_12_out, D5, D7);
  or or_13 (or_13_out, D6, D7);
  and and_16 (ALU_SELECT[2], D8, AT3);
  or or_14 (or_14_out, D4, D5);
  and and_17 (CARRY_LOAD, or_14_out, AT3);
  and and_18 (SHIFT_MODE_IN, AT2, DD);
  and and_19 (SHIFT_DATA_IN, AT3, DD);
  and and_20 (SHIFT_OUT, AT4, DD);
  and and_21 (ROTATE_MODE_IN, AT2, DE);
  and and_22 (ROTATE_DATA_IN, AT3, DE);
  and and_23 (ROTATE_OUT, AT4, DE);
  and and_24 (CONST_ZERO_OUT, AT3, D9);
  and and_25 (HLT, AT2, DF);
  or or_15 (or_15_out, D1, D2, D3, D4, D5, D6, D7, D8, D9);
  and and_26 (PC_IN, AT2, JUMP_COND);
  or or_16 (or_16_out, D1, D2, D3);
  or or_17 (RAM_OUT, and_12_out, IR_IN);
  and and_27 (and_27_out, or_8_out, AT3);
  and and_28 (A_OUT, or_10_out, AT3);
  and and_29 (ALU_OUT, or_11_out, AT3);
  and and_30 (ALU_SELECT[0], or_12_out, AT3);
  and and_31 (ALU_SELECT[1], or_13_out, AT3);
  or or_18 (or_18_out, or_3_out, or_4_out, and_10_out, and_11_out);
  or or_19 (or_19_out, or_6_out, or_7_out);
  or or_20 (A_IN, and_27_out, and_14_out);
  and and_32 (and_32_out, AT3, D0);
  and and_33 (and_33_out, AT4, or_15_out);
  and and_34 (and_34_out, AT3, or_1_out);
  and and_35 (and_35_out, AT5, or_2_out);
  and and_36 (PC_INC, or_18_out, AT2);
  and and_37 (and_37_out, AT2, or_16_out);
  and and_38 (OPERAND_OUT, or_19_out, AT2);
  or or_21 (JUMP_COND, JC_TAKEN, JNZ_TAKEN, DA);
  or or_22 (MAR_IN, and_37_out, PC_OUT);
  or or_23 (or_23_out, and_32_out, and_33_out, and_34_out, and_35_out);
  or or_24 (TIMING_RESET, or_23_out, debug, reset);

  assign PC_RESET = reset;

  // Other names for the same wires on the sheet: AT0 = PC_OUT; AT1 = IR_IN

  // Notes on the sheet:
  //   input pins
  //   Instruction
  //   NOP
  //   LDA addr 
  //   LDB addr 
  //   STA addr 
  //   ADD 
  //   SUB
  //   AND
  //   OR
  //   XOR
  //   CLR
  //   JMP addr
  //   JC addr 
  //   JNZ addr 
  //   SHIFT D, N 
  //   ROTATE D, N
  //   HLT
  //   Opcode Rails
  //   PC group
  //   Active Timing Rails
  //   Memory group
  //   Flag Rails
  //   output pins
  //   Register/ALU group
  //   Mode Rails
  //   JC TAKEN
  //   INC_GROUP_A
  //   INC_GROUP_B
  //   JC_NOT_TAKEN
  //   JNZ_NOT_TAKEN
  //   LOAD_INST
  //   LOAD_RAM_READ 
  //   OPERAND_GROUP_A
  //   ALU_S0
  //   ALU_S1
  //   ALU_S2
  //   NORMAL_GROUP
  //   JUMP_GROUP
  //   BIT_GROUP
  //   Shift/rotate group
  //   ADDRESS_INST
  //   ADDRESS_TO_MAR
  //   Jump condition
  //   INC_COND
  //   Miscellaneous
endmodule

module clock_control (
  input  CLK_RAW,
  input  HLT,
  output CPU_CLK
);

  wire not_1_out;

  not not_1 (not_1_out, HLT);
  and and_1 (CPU_CLK, CLK_RAW, not_1_out);
endmodule

module ram_loader_8bit (
  input  loader_clk,
  input  load_mode,
  input  load_reset,
  output [7:0] loader_bus_data,
  output loader_bus_en,
  output loader_mar_in,
  output loader_ram_wr,
  output loader_done,
  output [3:0] loader_address,
  output loader_phase
);

  wire ADDRESS_F, NOT_DONE, NOT_PHASE, NOT_RESET, or_1_out, phase_ff_D, WRITE_LAST;
  wire [7:0] ADDR8, RAM_DATA, RAW_BUS_DATA;

  D_Flip_Flop phase_ff (
    .D(phase_ff_D), .clk(loader_clk), .Q(loader_phase), .Qn(NOT_PHASE), .preset(1'b0), .reset(load_reset));
  Multiplexer #(.width(8)) multiplexer_1 (
    .in0({8{1'b0}}), .in1(RAW_BUS_DATA), .out(loader_bus_data), .sel(loader_bus_en));
  Multiplexer multiplexer_2 (.in0(loader_phase), .in1(NOT_PHASE), .out(phase_ff_D), .sel(loader_bus_en));
  and and_1 (loader_bus_en, load_mode, NOT_DONE, NOT_RESET);
  and and_2 (WRITE_LAST, loader_bus_en, loader_phase, ADDRESS_F);
  or or_1 (or_1_out, loader_done, WRITE_LAST);
  Multiplexer #(.width(8)) multiplexer_3 (.in0(ADDR8), .in1(RAM_DATA), .out(RAW_BUS_DATA), .sel(loader_phase));
  Comparator #(.mode("unsigned"), .width(4)) comparator_1 (
    .a(loader_address), .b(4'b1111), .eq(ADDRESS_F));  // open: gt, lt
  Counter #(.max('hf), .width(4)) counter_1 (
    .clr(load_reset), .load(1'b0), .up(1'b1), .count(loader_ram_wr), .clk(loader_clk), .D(4'b0000),
    .Q(loader_address));  // open: carry
  D_Flip_Flop done_ff (
    .D(or_1_out), .clk(loader_clk), .Q(loader_done), .Qn(NOT_DONE), .preset(1'b0), .reset(load_reset));
  and and_3 (loader_mar_in, loader_bus_en, NOT_PHASE);
  RAM #(.addrWidth(4)) ram_1 (
    .addr(loader_address), .we(1'b0), .oe(1'b1), .clk(loader_clk), .dout(RAM_DATA));  // open: din
  not not_1 (NOT_RESET, load_reset);
  assign ADDR8 = {{4{1'b0}}, loader_address};  // Bit_Extender bit_extender_1
  and and_4 (loader_ram_wr, loader_bus_en, loader_phase);

  // Other names for the same wires on the sheet: ACTIVE = loader_bus_en; ADDR4[3:0] = loader_address;
  //   clk = loader_clk; COUNT_ENABLE = loader_ram_wr; DONE_FF_Q = loader_done; PHASE = loader_phase
endmodule
